// Logisim project BCG16CPU.circ as structural Verilog: 7 circuits, main circuit main
module main (
);

  wire button_1_out, clock_1_out;
  wire [7:0] rom_1_data;
  wire [31:0] cpu_1_rom_address;

  Clock clock_1 (.out(clock_1_out));
  Button button_1 (.out(button_1_out));
  CPU cpu_1 (
    .Databus_IN(rom_1_data), .IRQ_B(1'b1), .CLK(clock_1_out), .CLS(button_1_out),
    .ROM_ADDRESS(cpu_1_rom_address));
  ROM #(.addrWidth(24)) rom_1 (.addr(cpu_1_rom_address[23:0]), .data(rom_1_data));

  // Notes on the sheet:
  //   contents of rom_1 (hex, n*v repeats v):
  //   20 0 aa
endmodule

module CPU (
  input  [7:0] Databus_IN,
  input  IRQ_B,
  input  CLK,
  input  CLS,
  output [31:0] ROM_ADDRESS
);

  wire d_ff_1_q, decode_1_inc_register, decode_1_load_register, IRQ_ENABLE, not_1_out, not_2_out, POST;
  wire [7:0] decode_1_rs;
  wire [15:0] decode_1_databus_out;

  not not_1 (not_1_out, IRQ_B);
  Counter #(.max('h3), .width(4)) counter_1 (
    .count(not_2_out), .carry(POST), .up(1'b1), .clk(CLK));  // open: load, D, Q, clr
  not not_2 (not_2_out, POST);
  D_Flip_Flop d_ff_1 (.D(not_1_out), .clk(CLK), .Q(d_ff_1_q), .preset(not_2_out), .reset(CLS));  // open: Qn
  not not_3 (IRQ_ENABLE, d_ff_1_q);
  Decode decode_1 (
    .Databus(Databus_IN), .CLK(CLK), .CLS(CLS), .RS(decode_1_rs), .DataBus_Out(decode_1_databus_out[7:0]),
    .Load_Register(decode_1_load_register), .Inc_Register(decode_1_inc_register));
  Registers registers_1 (
    .DataBus(decode_1_databus_out[7:0]), .RS(decode_1_rs), .Enable(1'b1), .Write(decode_1_load_register),
    .Inc(decode_1_inc_register), .Dec(1'b0), .Instr_Output(1'b0), .CLK(CLK), .CLS(CLS),
    .M_OUT(decode_1_databus_out), .M_PCOUT(ROM_ADDRESS));  // open: M_ABOUT, M_CDOUT, M_HLOUT, M_FOUT, M_MBOUT
  // Pins of 8 and 16 bits meet at decode_1_databus_out
endmodule

module Register8Bits (
  input  [7:0] DataBus,
  input  Enable,
  input  All_registers,
  input  Write,
  input  Inc,
  input  Dec,
  input  CLK,
  input  CLS,
  input  Output_Enable,
  input  Lowoverflowing,
  output Overflow,
  output [7:0] M_OUT
);

  wire and_1_out, and_2_out, and_3_out, and_4_out, and_5_out, and_6_out, and_7_out, counter_1_carry,
       or_1_out, or_2_out, or_3_out, or_4_out, or_5_out, or_6_out;
  wire [7:0] counter_1_q;

  and and_1 (and_1_out, All_registers, Lowoverflowing);
  or or_1 (or_1_out, Dec, Inc);
  and and_2 (and_2_out, Enable, ~and_1_out);  // AND_Gate
  and and_3 (and_3_out, or_1_out, and_2_out);
  and and_4 (and_4_out, and_2_out, or_2_out);
  or or_2 (or_2_out, Inc, ~Dec);  // OR_Gate
  and and_5 (and_5_out, and_2_out, Write);
  and and_6 (and_6_out, All_registers, Lowoverflowing);
  or or_3 (or_3_out, and_4_out, and_6_out);
  or or_4 (or_4_out, and_3_out, and_6_out);
  or or_5 (or_5_out, and_6_out, CLK);
  Counter counter_1 (
    .clr(CLS), .load(and_5_out), .up(or_3_out), .count(or_4_out), .clk(or_5_out), .D(DataBus),
    .carry(counter_1_carry), .Q(counter_1_q));
  and and_7 (and_7_out, and_2_out, ~or_1_out, ~Write);  // AND_Gate
  and and_8 (Overflow, and_2_out, counter_1_carry);
  assign M_OUT = or_6_out ? counter_1_q : 8'bz;  // Controlled_Buffer controlled_buffer_1
  or or_6 (or_6_out, and_7_out, Output_Enable);
endmodule

module Register16Bits (
  input  [15:0] DataBus,
  input  Enable_ALL,
  input  Enable_LOW,
  input  Enable_HIGH,
  input  Enable,
  input  Write,
  input  Inc,
  input  Dec,
  input  CLK,
  input  CLS,
  input  OutputEnable,
  output [15:0] M_out,
  output [7:0] M_out_HIGH,
  output [7:0] M_out_LOW
);

  wire and_1_out, and_2_out, and_3_out, not_1_out, not_2_out, or_1_out, or_2_out, or_3_out, or_4_out,
       or_5_out;
  wire [7:0] controlled_buffer_1_out, controlled_buffer_3_out, counter_1_q, counter_1_q_2;

  or or_1 (or_1_out, Inc, Dec);
  or or_2 (or_2_out, Write, Inc, Dec);
  or or_3 (or_3_out, Enable_HIGH, Enable_ALL);
  or or_4 (or_4_out, Enable_ALL, Enable_LOW);
  and and_1 (and_1_out, or_5_out, or_1_out, ~Write);  // AND_Gate
  or or_5 (or_5_out, Inc, ~Dec);  // OR_Gate
  not not_1 (not_1_out, or_3_out);
  not not_2 (not_2_out, or_4_out);
  and and_2 (and_2_out, and_1_out, Enable);
  assign controlled_buffer_1_out = Enable_ALL ? DataBus[15:8] : 8'bz;  // Controlled_Buffer controlled_buffer_1
  assign controlled_buffer_1_out = Enable_HIGH ? DataBus[7:0] : 8'bz;  // Controlled_Buffer controlled_buffer_2
  assign controlled_buffer_3_out = Enable_LOW ? DataBus[7:0] : 8'bz;  // Controlled_Buffer controlled_buffer_3
  assign controlled_buffer_3_out = Enable_ALL ? DataBus[7:0] : 8'bz;  // Controlled_Buffer controlled_buffer_4
  and and_3 (and_3_out, Enable, or_2_out);
  assign controlled_buffer_1_out = not_1_out ? counter_1_q_2 : 8'bz;  // Controlled_Buffer controlled_buffer_5
  assign controlled_buffer_3_out = not_2_out ? counter_1_q : 8'bz;  // Controlled_Buffer controlled_buffer_6
  Counter #(.max('hffff), .width(16)) counter_1 (
    .clr(CLS), .load(Write), .up(and_2_out), .count(and_3_out), .clk(CLK),
    .D({controlled_buffer_1_out, controlled_buffer_3_out}), .Q({counter_1_q_2, counter_1_q}));  // open: carry
  assign M_out = OutputEnable ? {counter_1_q_2, counter_1_q} : 16'bz;  // Controlled_Buffer controlled_buffer_7

  assign M_out_HIGH = M_out[15:8];
  assign M_out_LOW = M_out[7:0];
endmodule

module Register32Bit (
  input  [15:0] DataBus,
  input  Enable_LOW,
  input  Enable_HIGH,
  input  Enable,
  input  Write,
  input  Inc,
  input  Dec,
  input  CLK,
  input  CLS,
  output [31:0] M_out,
  output [15:0] M_out_HIGH,
  output [15:0] M_out_LOW
);

  wire and_1_out, and_2_out;
  wire [15:0] controlled_buffer_1_out, controlled_buffer_2_out;

  and and_1 (and_1_out, Enable_HIGH, Enable);
  and and_2 (and_2_out, Enable, Enable_LOW);
  assign controlled_buffer_1_out = Enable_HIGH ? DataBus : 16'bz;  // Controlled_Buffer controlled_buffer_1
  assign controlled_buffer_2_out = Enable_LOW ? DataBus : 16'bz;  // Controlled_Buffer controlled_buffer_2
  Register16Bits High (
    .OutputEnable(1'b1), .Enable_ALL(and_1_out), .Enable_LOW(1'b0), .Enable_HIGH(1'b0), .Enable(and_1_out),
    .Write(Write), .Inc(Inc), .Dec(Dec), .CLK(CLK), .CLS(CLS), .DataBus(controlled_buffer_1_out),
    .M_out(M_out[31:16]));  // open: M_out_HIGH, M_out_LOW
  Register16Bits Low (
    .OutputEnable(1'b1), .Enable_ALL(and_2_out), .Enable_LOW(1'b0), .Enable_HIGH(1'b0), .Enable(and_2_out),
    .Write(Write), .Inc(Inc), .Dec(Dec), .CLK(CLK), .CLS(CLS), .DataBus(controlled_buffer_2_out),
    .M_out(M_out[15:0]));  // open: M_out_HIGH, M_out_LOW

  assign M_out_HIGH = M_out[31:16];
  assign M_out_LOW = M_out[15:0];
endmodule

module Registers (
  input  [7:0] DataBus,
  input  [7:0] RS,
  input  Enable,
  input  Write,
  input  Inc,
  input  Dec,
  input  Instr_Output,
  input  CLK,
  input  CLS,
  output [31:0] M_ABOUT,
  output [31:0] M_CDOUT,
  output [15:0] M_OUT,
  output [31:0] M_HLOUT,
  output [31:0] M_PCOUT,
  output [15:0] M_FOUT,
  output [3:0] M_MBOUT
);

  wire and_1_out, and_2_out, and_3_out, demultiplexer_1_out0, demultiplexer_1_out1, demultiplexer_1_out2,
       demultiplexer_1_out3, demultiplexer_1_out4, demultiplexer_1_out5, demultiplexer_1_out6,
       demultiplexer_1_out7, demultiplexer_1_out8, demultiplexer_1_out9, demultiplexer_1_out10,
       demultiplexer_1_out15, demultiplexer_2_out0, demultiplexer_2_out1, demultiplexer_2_out2,
       demultiplexer_2_out3;
  wire [7:0] MB_m_out;
  wire [15:0] A_m_out, B_m_out, C_m_out, D_m_out, X_m_out, Y_m_out;
  wire [15:8] undriven;

  Demultiplexer #(.select(4)) demultiplexer_1 (
    .out0(demultiplexer_1_out0), .out1(demultiplexer_1_out1), .out2(demultiplexer_1_out2),
    .out3(demultiplexer_1_out3), .out4(demultiplexer_1_out4), .out5(demultiplexer_1_out5),
    .out6(demultiplexer_1_out6), .out7(demultiplexer_1_out7), .out8(demultiplexer_1_out8),
    .out9(demultiplexer_1_out9), .out10(demultiplexer_1_out10), .out15(demultiplexer_1_out15), .in(Enable),
    .sel(RS[3:0]));  // open: out11, out12, out13, out14
  Demultiplexer #(.select(2)) demultiplexer_2 (
    .out0(demultiplexer_2_out0), .out1(demultiplexer_2_out1), .out2(demultiplexer_2_out2),
    .out3(demultiplexer_2_out3), .in(Enable), .sel(RS[5:4]));
  Demultiplexer #(.select(2)) demultiplexer_3 (.in(Enable), .sel(RS[7:6]));  // open: out0, out1, out2, out3
  and and_1 (and_1_out, demultiplexer_2_out3, demultiplexer_1_out0);
  and and_2 (and_2_out, demultiplexer_2_out3, demultiplexer_1_out1);
  and and_3 (and_3_out, Instr_Output, Enable);
  Register16Bits A (
    .OutputEnable(and_1_out), .Enable_ALL(demultiplexer_2_out0), .Enable_LOW(demultiplexer_2_out1),
    .Enable_HIGH(demultiplexer_2_out2), .Enable(demultiplexer_1_out0), .Write(Write), .Inc(Inc), .Dec(Dec),
    .CLK(CLK), .CLS(CLS), .DataBus({undriven, DataBus}), .M_out(A_m_out));  // open: M_out_HIGH, M_out_LOW
  Register16Bits B (
    .OutputEnable(and_1_out), .Enable_ALL(demultiplexer_2_out0), .Enable_LOW(demultiplexer_2_out1),
    .Enable_HIGH(demultiplexer_2_out2), .Enable(demultiplexer_1_out1), .Write(Write), .Inc(Inc), .Dec(Dec),
    .CLK(CLK), .CLS(CLS), .DataBus({undriven, DataBus}), .M_out(B_m_out));  // open: M_out_HIGH, M_out_LOW
  Register16Bits C (
    .OutputEnable(and_2_out), .Enable_ALL(demultiplexer_2_out0), .Enable_LOW(demultiplexer_2_out1),
    .Enable_HIGH(demultiplexer_2_out2), .Enable(demultiplexer_1_out2), .Write(Write), .Inc(Inc), .Dec(Dec),
    .CLK(CLK), .CLS(CLS), .DataBus({undriven, DataBus}), .M_out(C_m_out));  // open: M_out_HIGH, M_out_LOW
  Register16Bits D (
    .OutputEnable(and_2_out), .Enable_ALL(demultiplexer_2_out0), .Enable_LOW(demultiplexer_2_out1),
    .Enable_HIGH(demultiplexer_2_out2), .Enable(demultiplexer_1_out3), .Write(Write), .Inc(Inc), .Dec(Dec),
    .CLK(CLK), .CLS(CLS), .DataBus({undriven, DataBus}), .M_out(D_m_out));  // open: M_out_HIGH, M_out_LOW
  Register16Bits X (
    .OutputEnable(and_2_out), .Enable_ALL(demultiplexer_2_out0), .Enable_LOW(demultiplexer_2_out1),
    .Enable_HIGH(demultiplexer_2_out2), .Enable(demultiplexer_1_out4), .Write(Write), .Inc(Inc), .Dec(Dec),
    .CLK(CLK), .CLS(CLS), .DataBus({undriven, DataBus}), .M_out(X_m_out));  // open: M_out_HIGH, M_out_LOW
  Register16Bits Y (
    .OutputEnable(and_2_out), .Enable_ALL(demultiplexer_2_out0), .Enable_LOW(demultiplexer_2_out1),
    .Enable_HIGH(demultiplexer_2_out2), .Enable(demultiplexer_1_out5), .Write(Write), .Inc(Inc), .Dec(Dec),
    .CLK(CLK), .CLS(CLS), .DataBus({undriven, DataBus}), .M_out(Y_m_out));  // open: M_out_HIGH, M_out_LOW
  Register32Bit HL (
    .Enable_LOW(demultiplexer_2_out1), .Enable_HIGH(demultiplexer_2_out2), .Enable(demultiplexer_1_out6),
    .Write(Write), .Inc(Inc), .Dec(Dec), .CLK(CLK), .CLS(CLS), .DataBus({undriven, DataBus}), .M_out(M_HLOUT));  // open: M_out_HIGH, M_out_LOW
  Register32Bit PC (
    .Enable_LOW(demultiplexer_2_out1), .Enable_HIGH(demultiplexer_2_out2), .Enable(demultiplexer_1_out7),
    .Write(Write), .Inc(Inc), .Dec(Dec), .CLK(CLK), .CLS(CLS), .DataBus({undriven, DataBus}), .M_out(M_PCOUT));  // open: M_out_HIGH, M_out_LOW
  Register16Bits F (
    .OutputEnable(and_2_out), .Enable_ALL(demultiplexer_2_out0), .Enable_LOW(1'b0), .Enable_HIGH(1'b0),
    .Enable(demultiplexer_1_out8), .Write(Write), .Inc(Inc), .Dec(Dec), .CLK(CLK), .CLS(CLS),
    .DataBus({undriven, DataBus}), .M_out(M_FOUT));  // open: M_out_HIGH, M_out_LOW
  Register32Bit AF (
    .Enable_LOW(demultiplexer_2_out1), .Enable_HIGH(demultiplexer_2_out2), .Enable(demultiplexer_1_out9),
    .Write(Write), .Inc(Inc), .Dec(Dec), .CLK(CLK), .CLS(CLS), .DataBus({undriven, DataBus}));  // open: M_out, M_out_HIGH, M_out_LOW
  Register32Bit BF (
    .Enable_LOW(demultiplexer_2_out1), .Enable_HIGH(demultiplexer_2_out2), .Enable(demultiplexer_1_out10),
    .Write(Write), .Inc(Inc), .Dec(Dec), .CLK(CLK), .CLS(CLS), .DataBus({undriven, DataBus}));  // open: M_out, M_out_HIGH, M_out_LOW
  assign M_ABOUT = and_1_out ? {B_m_out, A_m_out} : 32'bz;  // Controlled_Buffer controlled_buffer_1
  assign M_CDOUT = and_2_out ? {D_m_out, C_m_out} : 32'bz;  // Controlled_Buffer controlled_buffer_2
  Bit_Extender #(.out_width(4)) bit_extender_1 (.in(MB_m_out), .out(M_MBOUT));
  Register8Bits MB (
    .Enable(demultiplexer_1_out15), .Write(Write), .Inc(Inc), .Dec(Dec), .CLK(CLK), .CLS(CLS),
    .DataBus(DataBus), .M_OUT(MB_m_out));  // open: All_registers, Lowoverflowing, Output_Enable, Overflow
  Multiplexer #(.disabled("Z"), .enable("true"), .select(4), .width(16)) multiplexer_1 (
    .in0(A_m_out), .in1(B_m_out), .in2(C_m_out), .in3(D_m_out), .in4(X_m_out), .in5(Y_m_out), .in8(M_FOUT),
    .out(M_OUT), .sel(RS[3:0]), .en(and_3_out));  // open: in6, in7, in9, in10, in11, in12, in13, in14, in15
  // Pins of 8 and 16 bits meet at {undriven, DataBus}
endmodule

module Decode (
  input  [7:0] Databus,
  input  CLK,
  input  CLS,
  output [7:0] RS,
  output [7:0] DataBus_Out,
  output Load_Register,
  output Inc_Register
);

  wire and_1_out, Arg1_reg, comparator_1_eq, comparator_2_eq, decoder_1_out0, decoder_1_out1, decoder_1_out2,
       decoder_1_out3, decoder_1_out4, decoder_1_out5, decoder_1_out6, decoder_1_out7, decoder_1_out8,
       decoder_1_out9, decoder_1_out10, decoder_1_out11, decoder_1_out12, decoder_1_out13, decoder_1_out14,
       decoder_1_out15, EI, LARG, not_1_out, not_2_out, or_1_out, or_2_out, Use_Arg_Reg;
  wire [3:0] Arg1, Arg2;
  wire [7:0] Arg_Reg_O, ArgumentRegister_q, controlled_buffer_2_out, counter_1_q, pull_resistor_1_node,
       pull_resistor_2_node, register_1_q;
  wire [31:0] rom_1_data;

  Demultiplexer #(.select(4)) demultiplexer_1 (
    .out2(Arg1_reg), .in(1'b1), .sel(Arg1));  // open: out0, out1, out3, out4, out5, out6, out7, out8, out9, out10, out11, out12, out13, out14, out15
  and and_1 (and_1_out, EI, ~CLK);  // AND_Gate
  Register register_1 (.D(Databus), .en(comparator_1_eq), .Q(register_1_q), .clk(CLK), .clr(or_1_out));
  or or_1 (or_1_out, CLS, and_1_out);
  Pull_Resistor pull_resistor_1 (.node(pull_resistor_1_node));
  Comparator comparator_1 (.a(pull_resistor_1_node), .b(register_1_q), .eq(comparator_1_eq));  // open: gt, lt
  buf or_2 (or_2_out, Use_Arg_Reg);  // OR_Gate
  Register ArgumentRegister (.D(Databus), .en(LARG), .clk(CLK), .Q(ArgumentRegister_q));  // open: clr
  Counter counter_1 (.count(not_1_out), .Q(counter_1_q), .up(1'b1), .clk(CLK), .clr(or_1_out));  // open: load, D, carry
  not not_1 (not_1_out, comparator_1_eq);
  assign Arg_Reg_O = Arg1_reg ? controlled_buffer_2_out : 8'bz;  // Controlled_Buffer controlled_buffer_1
  assign controlled_buffer_2_out = or_2_out ? ArgumentRegister_q : 8'bz;  // Controlled_Buffer controlled_buffer_2
  Pull_Resistor pull_resistor_2 (.node(pull_resistor_2_node));
  ROM #(.addrWidth(24), .dataWidth(32)) rom_1 (
    .addr({register_1_q, pull_resistor_2_node, counter_1_q}),
    .data({rom_1_data[31:25], Use_Arg_Reg, Arg1, Arg2, rom_1_data[15:0]}));
  Decoder #(.select(4)) decoder_1 (
    .out0(decoder_1_out0), .out1(decoder_1_out1), .out2(decoder_1_out2), .out3(decoder_1_out3),
    .out4(decoder_1_out4), .out5(decoder_1_out5), .out6(decoder_1_out6), .out7(decoder_1_out7),
    .out8(decoder_1_out8), .out9(decoder_1_out9), .out10(decoder_1_out10), .out11(decoder_1_out11),
    .out12(decoder_1_out12), .out13(decoder_1_out13), .out14(decoder_1_out14), .out15(decoder_1_out15),
    .sel(rom_1_data[7:4]), .en(not_1_out));
  assign RS = not_2_out ? rom_1_data[15:8] : 8'bz;  // Controlled_Buffer controlled_buffer_3
  not not_2 (not_2_out, comparator_2_eq);
  Comparator comparator_2 (.a({8{1'b1}}), .b(rom_1_data[15:8]), .eq(comparator_2_eq));  // open: gt, lt
  Decoder #(.select(4)) decoder_2 (
    .out0(Load_Register), .sel(rom_1_data[3:0]), .en(decoder_1_out0));  // open: out1, out2, out3, out4, out5, out6, out7, out8, out9, out10, out11, out12, out13, out14, out15
  Decoder #(.select(4)) decoder_3 (
    .sel(rom_1_data[3:0]), .en(decoder_1_out1));  // open: out0, out1, out2, out3, out4, out5, out6, out7, out8, out9, out10, out11, out12, out13, out14, out15
  Decoder #(.select(4)) decoder_4 (
    .sel(rom_1_data[3:0]), .en(decoder_1_out2));  // open: out0, out1, out2, out3, out4, out5, out6, out7, out8, out9, out10, out11, out12, out13, out14, out15
  Decoder #(.select(4)) decoder_5 (
    .out15(Inc_Register), .sel(rom_1_data[3:0]), .en(decoder_1_out3));  // open: out0, out1, out2, out3, out4, out5, out6, out7, out8, out9, out10, out11, out12, out13, out14
  Decoder #(.select(4)) decoder_6 (
    .sel(rom_1_data[3:0]), .en(decoder_1_out4));  // open: out0, out1, out2, out3, out4, out5, out6, out7, out8, out9, out10, out11, out12, out13, out14, out15
  Decoder #(.select(4)) decoder_7 (
    .sel(rom_1_data[3:0]), .en(decoder_1_out5));  // open: out0, out1, out2, out3, out4, out5, out6, out7, out8, out9, out10, out11, out12, out13, out14, out15
  Decoder #(.select(4)) decoder_8 (
    .sel(rom_1_data[3:0]), .en(decoder_1_out6));  // open: out0, out1, out2, out3, out4, out5, out6, out7, out8, out9, out10, out11, out12, out13, out14, out15
  Decoder #(.select(4)) decoder_9 (
    .sel(rom_1_data[3:0]), .en(decoder_1_out7));  // open: out0, out1, out2, out3, out4, out5, out6, out7, out8, out9, out10, out11, out12, out13, out14, out15
  Decoder #(.select(4)) decoder_10 (
    .sel(rom_1_data[3:0]), .en(decoder_1_out8));  // open: out0, out1, out2, out3, out4, out5, out6, out7, out8, out9, out10, out11, out12, out13, out14, out15
  Decoder #(.select(4)) decoder_11 (
    .sel(rom_1_data[3:0]), .en(decoder_1_out9));  // open: out0, out1, out2, out3, out4, out5, out6, out7, out8, out9, out10, out11, out12, out13, out14, out15
  Decoder #(.select(4)) decoder_12 (
    .sel(rom_1_data[3:0]), .en(decoder_1_out10));  // open: out0, out1, out2, out3, out4, out5, out6, out7, out8, out9, out10, out11, out12, out13, out14, out15
  Decoder #(.select(4)) decoder_13 (
    .sel(rom_1_data[3:0]), .en(decoder_1_out11));  // open: out0, out1, out2, out3, out4, out5, out6, out7, out8, out9, out10, out11, out12, out13, out14, out15
  Decoder #(.select(4)) decoder_14 (
    .sel(rom_1_data[3:0]), .en(decoder_1_out12));  // open: out0, out1, out2, out3, out4, out5, out6, out7, out8, out9, out10, out11, out12, out13, out14, out15
  Decoder #(.select(4)) decoder_15 (
    .sel(rom_1_data[3:0]), .en(decoder_1_out13));  // open: out0, out1, out2, out3, out4, out5, out6, out7, out8, out9, out10, out11, out12, out13, out14, out15
  Decoder #(.select(4)) decoder_16 (
    .sel(rom_1_data[3:0]), .en(decoder_1_out14));  // open: out0, out1, out2, out3, out4, out5, out6, out7, out8, out9, out10, out11, out12, out13, out14, out15
  Decoder #(.select(4)) decoder_17 (
    .out0(LARG), .out15(EI), .sel(rom_1_data[3:0]), .en(decoder_1_out15));  // open: out1, out2, out3, out4, out5, out6, out7, out8, out9, out10, out11, out12, out13, out14
  assign RS = Arg1_reg ? Arg_Reg_O : 8'bz;  // Controlled_Buffer controlled_buffer_4

  assign DataBus_Out = Databus;

  // Notes on the sheet:
  //   contents of rom_1 (hex, n*v repeats v):
  //   8192*0 173f f0 173f 120ff00 173f ff 250*0 73f f0 120ff00 253*0 73f
endmodule
